// Logisim project 4-bit ripple asynchronous counter.circ as structural Verilog: 1 circuit, main circuit main
module main (
  input  Clk,
  input  En
);

  wire clock_1_out, t_ff_1_q, t_ff_1_qn, t_ff_2_q, t_ff_2_qn, t_ff_3_q, t_ff_3_qn, t_ff_4_q;

  Clock clock_1 (.out(clock_1_out));
  LED led_1 (.in(t_ff_1_q));
  T_Flip_Flop t_ff_1 (.clk(clock_1_out), .T(Clk), .Q(t_ff_1_q), .Qn(t_ff_1_qn), .en(En));  // open: preset, reset
  LED led_2 (.in(t_ff_2_q));
  T_Flip_Flop t_ff_2 (.clk(t_ff_1_qn), .T(Clk), .Q(t_ff_2_q), .Qn(t_ff_2_qn), .en(En));  // open: preset, reset
  LED led_3 (.in(t_ff_3_q));
  T_Flip_Flop t_ff_3 (.clk(t_ff_2_qn), .T(Clk), .Q(t_ff_3_q), .Qn(t_ff_3_qn), .en(En));  // open: preset, reset
  LED led_4 (.in(t_ff_4_q));
  T_Flip_Flop t_ff_4 (.clk(t_ff_3_qn), .T(Clk), .Q(t_ff_4_q), .en(En));  // open: Qn, preset, reset

  // Notes on the sheet:
  //   T0
  //   Q0
  //   Q1
  //   Q2
  //   Q3
endmodule
