// Logisim project 4-bit synchronous binary counter (using T flip-flops).circ as structural Verilog: 1 circuit, main circuit main
module main (
  input  T0,
  input  En
);

  wire and_1_out, and_2_out, clock_1_out, t_ff_1_q, t_ff_2_q, t_ff_3_q, t_ff_4_q;

  Clock clock_1 (.out(clock_1_out));
  LED led_1 (.in(t_ff_1_q));
  T_Flip_Flop t_ff_1 (.clk(clock_1_out), .T(T0), .Q(t_ff_1_q), .en(En));  // open: Qn, preset, reset
  LED led_2 (.in(t_ff_2_q));
  T_Flip_Flop t_ff_2 (.clk(clock_1_out), .T(t_ff_1_q), .Q(t_ff_2_q), .en(En));  // open: Qn, preset, reset
  and and_1 (and_1_out, t_ff_1_q, t_ff_2_q);
  LED led_3 (.in(t_ff_3_q));
  T_Flip_Flop t_ff_3 (.clk(clock_1_out), .T(and_1_out), .Q(t_ff_3_q), .en(En));  // open: Qn, preset, reset
  and and_2 (and_2_out, and_1_out, t_ff_3_q);
  T_Flip_Flop t_ff_4 (.clk(clock_1_out), .T(and_2_out), .Q(t_ff_4_q), .en(En));  // open: Qn, preset, reset
  LED led_4 (.in(t_ff_4_q));

  // Notes on the sheet:
  //   Clk
  //   Q0
  //   Q1
  //   Q2
  //   Q3
endmodule
