// Logisim project PIPO.circ as structural Verilog: 1 circuit, main circuit main
module main (
  input  In0,
  input  In1,
  input  In2,
  input  In3,
  input  En,
  input  Clear
);

  wire clock_1_out, d_ff_1_q, d_ff_2_q, d_ff_3_q, d_ff_4_q;

  Clock clock_1 (.out(clock_1_out));
  LED led_1 (.in(d_ff_1_q));
  D_Flip_Flop d_ff_1 (.clk(clock_1_out), .D(In0), .Q(d_ff_1_q), .en(En), .reset(Clear));  // open: Qn, preset
  LED led_2 (.in(d_ff_2_q));
  D_Flip_Flop d_ff_2 (.clk(clock_1_out), .D(In1), .Q(d_ff_2_q), .en(En), .reset(Clear));  // open: Qn, preset
  LED led_3 (.in(d_ff_3_q));
  D_Flip_Flop d_ff_3 (.clk(clock_1_out), .D(In2), .Q(d_ff_3_q), .en(En), .reset(Clear));  // open: Qn, preset
  LED led_4 (.in(d_ff_4_q));
  D_Flip_Flop d_ff_4 (.clk(clock_1_out), .D(In3), .Q(d_ff_4_q), .en(En), .reset(Clear));  // open: Qn, preset

  // Notes on the sheet:
  //   Clk
  //   Out0
  //   Out1
  //   Out2
  //   Out3
endmodule
