// Logisim project PISO.circ as structural Verilog: 1 circuit, main circuit main
module main (
  input  In0,
  input  In1,
  input  In2,
  input  In3,
  input  in_5,
  input  En,
  input  Clear
);

  wire and_1_out, and_2_out, and_3_out, and_4_out, and_5_out, and_6_out, clock_1_out, d_ff_1_q, d_ff_2_q,
       d_ff_3_q, d_ff_4_q, not_1_out, or_1_out, or_2_out, or_3_out;

  not not_1 (not_1_out, in_5);
  Clock clock_1 (.out(clock_1_out));
  and and_1 (and_1_out, d_ff_1_q, in_5);
  D_Flip_Flop d_ff_1 (.clk(clock_1_out), .D(In0), .Q(d_ff_1_q), .en(En), .reset(Clear));  // open: Qn, preset
  and and_2 (and_2_out, not_1_out, In1);
  or or_1 (or_1_out, and_1_out, and_2_out);
  D_Flip_Flop d_ff_2 (.clk(clock_1_out), .D(or_1_out), .Q(d_ff_2_q), .en(En), .reset(Clear));  // open: Qn, preset
  and and_3 (and_3_out, d_ff_2_q, in_5);
  and and_4 (and_4_out, not_1_out, In2);
  or or_2 (or_2_out, and_3_out, and_4_out);
  D_Flip_Flop d_ff_3 (.clk(clock_1_out), .D(or_2_out), .Q(d_ff_3_q), .en(En), .reset(Clear));  // open: Qn, preset
  and and_5 (and_5_out, d_ff_3_q, in_5);
  and and_6 (and_6_out, not_1_out, In3);
  or or_3 (or_3_out, and_5_out, and_6_out);
  LED led_1 (.in(d_ff_4_q));
  D_Flip_Flop d_ff_4 (.clk(clock_1_out), .D(or_3_out), .Q(d_ff_4_q), .en(En), .reset(Clear));  // open: Qn, preset

  // Notes on the sheet:
  //   Input
  //   Clk
  //   Out
endmodule
