// Logisim project SIPO.circ as structural Verilog: 1 circuit, main circuit main
module main (
  input  Input,
  input  En,
  input  Clear
);

  wire clock_1_out, d_ff_1_q, d_ff_2_q, d_ff_3_q, d_ff_4_q;

  Clock clock_1 (.out(clock_1_out));
  LED led_1 (.in(d_ff_1_q));
  D_Flip_Flop d_ff_1 (.clk(clock_1_out), .D(Input), .Q(d_ff_1_q), .en(En), .reset(Clear));  // open: Qn, preset
  LED led_2 (.in(d_ff_2_q));
  D_Flip_Flop d_ff_2 (.clk(clock_1_out), .D(d_ff_1_q), .Q(d_ff_2_q), .en(En), .reset(Clear));  // open: Qn, preset
  LED led_3 (.in(d_ff_3_q));
  D_Flip_Flop d_ff_3 (.clk(clock_1_out), .D(d_ff_2_q), .Q(d_ff_3_q), .en(En), .reset(Clear));  // open: Qn, preset
  LED led_4 (.in(d_ff_4_q));
  D_Flip_Flop d_ff_4 (.clk(clock_1_out), .D(d_ff_3_q), .Q(d_ff_4_q), .en(En), .reset(Clear));  // open: Qn, preset

  // Notes on the sheet:
  //   Clk
  //   Out3
endmodule
