// Logisim project SR Latch.circ as structural Verilog: 1 circuit, main circuit main
module main (
  input  R,
  input  S
);

  wire nor_1_out, nor_2_out;

  nor nor_1 (nor_1_out, R, nor_2_out);
  nor nor_2 (nor_2_out, nor_1_out, S);
  LED led_1 (.in(nor_1_out));
  LED led_2 (.in(nor_2_out));

  // Notes on the sheet:
  //   NOR1
  //   NOR2
  //   Q
  //   Q'
endmodule
